# Fritzing sketch JamesBrown (saved by Fritzing 0.8.5b)
breadboards: 1

parts:
  Part1 = Arduino Uno (Rev3)
  R1 = Temperature Sensor (Thermistor) [thermistor_type=NTC package=THT]
  R2 = Resistor [tolerance=±5% resistance=10k package=THT]
  Part2 = Humidity Temperature Sensor SHT15
  J1 = Piezo Speaker
  S1 = Toggle Switch [package=THT]
  LCD1 = LCD screen
  R3 = Resistor [tolerance=±5% resistance=1k package=THT]

nets:
  N1: Part1.A0, R1.pin_0, R2.Pin_1
  N2: Part1.A1, Part2.A0
  N3: Part1.D11_PWM/MOSI, LCD1.E
  N4: Part1.D12/MISO, LCD1.RS
  N5: Part1.D2, LCD1.DB7
  N6: Part1.D3_PWM, LCD1.DB6
  N7: Part1.D4, LCD1.DB5
  N8: Part1.D5_PWM, LCD1.DB4
  N9: Part1.D7, S1.COM
  5V: Part1.5V, R1.pin_1, Part2.VCC, LCD1.VDD, LCD1.LED+
  GND: Part1.GND, R2.Pin_0, Part2.GND, LCD1.VSS, LCD1.V0, LCD1.R/W, LCD1.LED-, R3.Pin_1
  N10: J1.pin1, R3.Pin_0
  N11: J1.pin2, S1.L2

custom parts:
  Humidity Temperature Sensor SHT15: Description: This is a simple breakout board for the SHT15 humidity sensor from Sensirion. The SHT15 digital humidity and temperature sensor is fully calibrated and offers high precision and excellent long-term stability at low cost. The digital CMOSens Technology integrates two sensors and readout circuitry on one single chip. These sensors are really impressive! Very sensitive and straight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
